// Logisim project tinycpu_2.circ as structural Verilog: 1 circuit, main circuit main
module main (
  input  in_1,
  input  in_2,
  input  in_3,
  input  in_4,
  input  in_5,
  input  in_6,
  input  in_7,
  input  in_8,
  input  in_9,
  input  in_10,
  input  [15:0] in_11,
  input  in_12,
  input  in_13,
  input  in_14,
  input  in_15,
  output [15:0] out_16,
  output [15:0] out_17,
  output [15:0] out_18,
  output [15:0] out_19,
  output [11:0] out_20,
  output [15:0] out_21,
  output [11:0] out_22,
  output [3:0] out_23,
  output [11:0] out_24,
  output [15:0] out_25,
  output [15:0] out_26,
  output [2:0] out_27,
  output [11:0] out_28
);

  wire A_WE, ALU_SUB, B_WE, C_WE, clk, clock_1_out, IS_ALU_ZERO, MAR_WE, MEM_HI_REG_RST, not_1_out, PC_WE,
       RAM_WE, STEP_REG_RST;
  wire [3:0] bit_extender_1_out, STEP_PLUS_1;
  wire [7:0] RAM_IN;
  wire [11:0] bit_extender_3_out, bit_extender_4_out, MAR_IN, MAR_PLUS_1, PC_IN, PC_PLUS_1;
  wire [15:0] C_REG, INST_ADDR_EXT, PC_REG_EXT;
  wire [31:3] CONTROL;

  Clock clock_1 (.out(clock_1_out));
  not not_1 (not_1_out, CONTROL[15]);
  and and_1 (clk, clock_1_out, not_1_out);
  Register REG_MEM_HI (.D(out_19[7:0]), .en(CONTROL[17]), .clk(clk), .Q(out_19[15:8]), .clr(MEM_HI_REG_RST));
  or or_1 (STEP_REG_RST, in_1, CONTROL[14]);
  Register #(.width(16)) REG_A (.D(out_25), .en(A_WE), .clk(clk), .Q(out_16), .clr(in_1));
  Register #(.width(16)) REG_B (.D(out_25), .en(B_WE), .clk(clk), .Q(out_17), .clr(in_1));
  Register #(.width(12)) REG_PC (.D(PC_IN), .en(PC_WE), .clk(clk), .Q(out_20), .clr(in_1));
  Register #(.width(12)) REG_MAR (.D(MAR_IN), .en(MAR_WE), .clk(clk), .Q(out_22), .clr(in_1));
  Register REG_INST_MSB (.D(out_25[7:0]), .en(CONTROL[9]), .clk(clk), .Q(out_21[15:8]), .clr(in_1));
  Register REG_INST_LSB (.D(out_25[7:0]), .en(CONTROL[10]), .clk(clk), .Q(out_21[7:0]), .clr(in_1));
  Register #(.width(4)) REG_STEP (.D(STEP_PLUS_1), .en(1'b1), .clk(clk), .Q(out_23), .clr(STEP_REG_RST));
  RAM #(.addrWidth(12), .asyncread("true")) ram_1 (
    .addr(out_22), .we(RAM_WE), .oe(1'b1), .clk(clk), .din(RAM_IN), .dout(out_19[7:0]));
  Adder #(.width(16)) adder_1 (.a(out_16), .b(out_17), .out(out_18), .cin(1'b0));  // open: cout
  assign bit_extender_1_out = {{3{1'b0}}, 1'b1};  // Bit_Extender bit_extender_1
  assign PC_REG_EXT = {{4{1'b0}}, out_20};  // Bit_Extender bit_extender_2
  or or_2 (MEM_HI_REG_RST, in_1, CONTROL[18]);
  Adder #(.width(4)) adder_2 (.a(out_23), .b(bit_extender_1_out), .out(STEP_PLUS_1), .cin(1'b0));  // open: cout
  Multiplexer #(.select(3), .width(16)) multiplexer_1 (
    .in0(out_16), .in1(out_17), .in2(C_REG), .in3(out_18), .in4(out_19), .in5(PC_REG_EXT),
    .in6(INST_ADDR_EXT), .in7(in_11), .out(out_25), .sel(out_27));
  nor nor_1 (IS_ALU_ZERO, out_18[0], out_18[1], out_18[2], out_18[3], out_18[4], out_18[5], out_18[6], out_18[7], out_18[8], out_18[9], out_18[10], out_18[11], out_18[12], out_18[13], out_18[14], out_18[15]);
  assign bit_extender_3_out = {{11{1'b0}}, 1'b1};  // Bit_Extender bit_extender_3
  assign bit_extender_4_out = {{11{1'b0}}, 1'b1};  // Bit_Extender bit_extender_4
  Adder #(.width(12)) adder_3 (.a(out_20), .b(bit_extender_3_out), .out(PC_PLUS_1), .cin(1'b0));  // open: cout
  or or_3 (PC_WE, CONTROL[7], CONTROL[8]);
  Multiplexer #(.select(2), .width(12)) multiplexer_2 (
    .in1(PC_PLUS_1), .in2(out_25[11:0]), .out(PC_IN), .sel(CONTROL[8:7]));  // open: in0, in3
  Adder #(.width(12)) adder_4 (.a(out_22), .b(bit_extender_4_out), .out(MAR_PLUS_1), .cin(1'b0));  // open: cout
  or or_4 (MAR_WE, CONTROL[3], CONTROL[4]);
  assign INST_ADDR_EXT = {{4{1'b0}}, out_21[11:0]};  // Bit_Extender bit_extender_5
  assign out_24[3:0] = {{3{1'b0}}, IS_ALU_ZERO};  // Bit_Extender bit_extender_6
  or or_5 (RAM_WE, CONTROL[5], CONTROL[6]);
  ROM #(.addrWidth(12), .dataWidth(32)) rom_1 (
    .addr({out_21[15:12], out_23, out_24[3:0]}),
    .data({CONTROL[31:17], ALU_SUB, CONTROL[15:14], out_27, CONTROL[10:3], C_WE, B_WE, A_WE}));
  Multiplexer #(.select(2), .width(12)) multiplexer_3 (
    .in1(MAR_PLUS_1), .in2(out_25[11:0]), .out(MAR_IN), .sel({CONTROL[3], CONTROL[4]}));  // open: in0, in3
  Multiplexer #(.select(2), .width(8)) multiplexer_4 (
    .in1(out_25[15:8]), .in2(out_25[7:0]), .out(RAM_IN), .sel(CONTROL[6:5]));  // open: in0, in3

  assign out_24[11:4] = {out_21[15:12], out_23};
  assign out_26 = out_25;
  assign out_28 = {out_21[15:12], out_23, out_24[3:0]};

  // Other names for the same wires on the sheet: PC_INC = CONTROL[7]; PC_JMP = CONTROL[8]; MAR_INC = CONTROL[4];
  //   MAR_BUS_WE = CONTROL[3]; RAM_MSB_WE = CONTROL[5]; RAM_LSB_WE = CONTROL[6]; A_REG[15:0] = out_16;
  //   ALU_OUT[15:0] = out_18; B_REG[15:0] = out_17; BUS_0_3[3:0] = out_25[3:0]; BUS_0_11[11:0] = out_25[11:0];
  //   BUS_LSB[7:0] = out_25[7:0]; THE_BUS[15:0] = out_25; BUS_4_7[3:0] = out_25[7:4]; BUS_8_11[3:0] = out_25[11:8];
  //   BUS_MSB[7:0] = out_25[15:8]; BUS_12_15[3:0] = out_25[15:12];
  //   CONTROL (some bits) = {ALU_SUB, out_27, C_WE, B_WE, A_WE}; INST_MSB_WE = CONTROL[9]; INST_LSB_WE = CONTROL[10];
  //   INST_STEP_RST = CONTROL[14]; HLT = CONTROL[15]; MEM_HI_WE = CONTROL[17]; MEM_HI_RST = CONTROL[18];
  //   INST_ADDR[11:0] = out_21[11:0]; INST_LSB_REG[7:0] = out_21[7:0]; INST_REG[15:0] = out_21;
  //   INST_REG_0_3[3:0] = out_21[3:0]; INST_REG_4_7[3:0] = out_21[7:4]; INST_MSB_REG[7:0] = out_21[15:8];
  //   INST_REG_8_11[3:0] = out_21[11:8]; MAN_REG[15:0] = in_11; MAR_REG[11:0] = out_22; PC_REG[11:0] = out_20;
  //   RAM_REG[7:0] = out_19[7:0]; RAM_REG_EXT[15:0] = out_19; MEM_HI_REG[7:0] = out_19[15:8]; BUS_SRC_0 = out_27[0];
  //   REG_SEL[2:0] = out_27; BUS_SRC_1 = out_27[1]; BUS_SRC_2 = out_27[2]; COND_FLAGS[3:0] = out_24[3:0];
  //   ROM_LOOKUP[11:0] = {out_21[15:12], out_23, out_24[3:0]}; STEP_REG[3:0] = out_23;
  //   INST_OPCODE[3:0] = out_21[15:12]; RST = in_1

  // Notes on the sheet:
  //   contents of rom_1 (hex, n*v repeats v):
  //   16*2808 16*2200 16*80 16*2808 16*2480 16*4000 160*0 16*2808 16*2200 16*80 16*2808 16*2480 16*3008
  //   16*20000 16*10 16*2001 16*4000 96*0 16*2808 16*2200 16*80 16*2808 16*2480 16*3008 16*20000 16*10
  //   16*2002 16*1801 16*4000 80*0 16*2808 16*2200 16*80 16*2808 16*2480 16*4000 160*0 16*2808 16*2200
  //   16*80 16*2808 16*2480 16*3008 16*20 16*10 16*40 16*4000 96*0 16*2808 16*2200 16*80 16*2808 16*2480
  //   16*3001 16*4000 144*0 16*2808 16*2200 16*80 16*2808 16*2480 16*3100 16*4000 144*0 16*2808 16*2200
  //   16*80 16*2808 16*2480 4000 3100 4000 3100 4000 3100 4000 3100 4000 3100 4000 3100 4000 3100 4000
  //   3100 17*4000 0 4000 0 4000 0 4000 0 4000 0 4000 0 4000 0 4000 0 4000 0 4000 0 4000 0 4000 0 4000 0
  //   4000 0 4000 0 4000 0 4000 0 4000 0 4000 0 4000 0 4000 0 4000 0 4000 0 4000 0 4000 0 4000 0 4000 0
  //   4000 0 4000 0 4000 0 4000 0 4000 0 4000 0 4000 0 4000 0 4000 0 4000 0 4000 0 4000 0 4000 0 4000 0
  //   4000 0 4000 0 4000 0 4000 0 4000 0 4000 0 4000 0 4000 0 4000 0 4000 0 4000 0 4000 0 4000 0 4000 0
  //   4000 0 4000 0 4000 0 4000 0 4000 0 4000 0 4000 0 4000 0 4000 0 4000 0 4000 0 4000 0 4000 0 4000 0
  //   4000 0 4000 0 4000 0 16*2808 16*2200 16*80 16*2808 16*2480 176*0 16*2808 16*2200 16*80 16*2808
  //   16*2480 176*0 16*2808 16*2200 16*80 16*2808 16*2480 176*0 16*2808 16*2200 16*80 16*2808 16*2480
  //   176*0 16*2808 16*2200 16*80 16*2808 16*2480 176*0 16*2808 16*2200 16*80 16*2808 16*2480 176*0
  //   16*2808 16*2200 16*80 16*2808 16*2480 176*0 16*2808 16*2200 16*80 16*2808 16*2480 16*8000
endmodule
